// Logisim project PipelinedMips.circ as structural Verilog: 4 circuits, main circuit main
module main (
);

  wire ALUSrcA, ALUSrcB, Clock, MemtoReg, RegDst, RegWrite, zero;
  wire [3:0] ALUCtl;
  wire [4:0] multiplexer_2_out, Shamt;
  wire [5:0] Funct, Opcode;
  wire [7:0] adder_1_out, bit_extender_2_out;
  wire [25:11] IR_q;
  wire [31:0] A_q, alu_1_aluresult, ALUout_q, bit_extender_1_out, bit_extender_3_out, multiplexer_1_out,
       multiplexer_3_out, multiplexer_4_out, ram_1_data, register_1_q, registerfile_1_read_data1,
       registerfile_1_read_data2, Store, undriven, undriven_2, undriven_3;

  assign bit_extender_1_out = {{24{1'b0}}, adder_1_out};  // Bit_Extender bit_extender_1
  Register #(.width(32)) register_1 (.D(bit_extender_1_out), .Q(register_1_q), .clk(Clock));  // open: en, clr
  Bit_Extender #(.in_width(32), .out_width(8)) bit_extender_2 (.in(register_1_q), .out(bit_extender_2_out));
  Adder adder_1 (.a(8'h4), .b(bit_extender_2_out), .out(adder_1_out));  // open: cin, cout
  Clock clock_1 (.out(Clock));
  RAM #(.dataWidth(32)) ram_1 (.addr(bit_extender_2_out), .data(ram_1_data));  // open: sel, clk, ld, clr
  Register #(.width(32)) IR (.D(ram_1_data), .Q({Opcode, IR_q, Shamt, Funct}), .clk(Clock));  // open: en, clr
  MultiCycleMips_CorrectALU_RegisterFile registerfile_1 (
    .WriteData(multiplexer_1_out), .ReadReg2(IR_q[20:16]), .RegWrite(RegWrite), .WriteReg(multiplexer_2_out),
    .Read_Data2(registerfile_1_read_data2), .Read_Data1(registerfile_1_read_data1), .clock(Clock),
    .Read_Reg1(IR_q[25:21]));
  Multiplexer #(.width(32), .enable("false")) multiplexer_1 (
    .in0(undriven_2), .in1(undriven), .out(multiplexer_1_out), .sel(MemtoReg));
  Multiplexer #(.width(5), .enable("false")) multiplexer_2 (
    .in0(IR_q[20:16]), .in1(IR_q[15:11]), .out(multiplexer_2_out), .sel(RegDst));
  assign bit_extender_3_out = {{16{IR_q[15]}}, {IR_q[15:11], Shamt, Funct}};  // Bit_Extender bit_extender_3
  Register #(.width(32)) A (.D(registerfile_1_read_data1), .Q(A_q), .clk(Clock));  // open: en, clr
  Register #(.width(32)) B (.D(registerfile_1_read_data2), .Q(Store), .clk(Clock));  // open: en, clr
  Multiplexer #(.width(32), .enable("false")) multiplexer_3 (
    .in0(undriven_3), .in1(A_q), .out(multiplexer_3_out), .sel(ALUSrcA));
  Multiplexer #(.width(32), .enable("false")) multiplexer_4 (
    .in0(Store), .in1(bit_extender_3_out), .out(multiplexer_4_out), .sel(ALUSrcB));
  MultiCycleMips_CorrectALU_ALU alu_1 (
    .ALUCtl(ALUCtl), .A(multiplexer_3_out), .B(multiplexer_4_out), .ALUResult(alu_1_aluresult), .Zero(zero),
    .SHamt(Shamt));  // open: Overflow
  Register #(.width(32)) ALUout (.D(alu_1_aluresult), .Q(ALUout_q), .clk(Clock));  // open: en, clr
endmodule

module _32bit (
  input  Add_Sub_control,
  input  [31:0] in_2,
  input  [31:0] in_3,
  output [31:0] out_4,
  output carry_out
);

  wire adder_1_cout, subtractor_1_bout;
  wire [31:0] adder_1_out, subtractor_1_out;

  Adder #(.width(32)) adder_1 (.a(in_2), .b(in_3), .out(adder_1_out), .cout(adder_1_cout));  // open: cin
  Subtractor #(.width(32)) subtractor_1 (
    .a(in_2), .b(in_3), .out(subtractor_1_out), .bout(subtractor_1_bout));  // open: bin
  Multiplexer #(.width(32), .enable("false")) multiplexer_1 (
    .in0(adder_1_out), .in1(subtractor_1_out), .out(out_4), .sel(Add_Sub_control));
  Multiplexer #(.enable("false")) multiplexer_2 (
    .in0(adder_1_cout), .in1(subtractor_1_bout), .out(carry_out), .sel(Add_Sub_control));
endmodule

module ALU (
  input  [3:0] ALUCtl,
  input  [31:0] A,
  input  [31:0] B,
  input  [4:0] SHamt,
  output [31:0] ALUResult,
  output Zero,
  output Overflow
);

  wire and_2_out, and_3_out, comparator_1_lt, not_1_out, not_2_out, not_4_out, not_5_out, not_6_out,
       or_2_out, or_3_out, xor_1_out;
  wire [31:0] AND_out, bit_extender_1_out, multiplexer_1_out, multiplexer_2_out, multiplexer_4_out,
       n32bit_1_out_4, not_3_out, OR_out, shifter_1_out, shifter_2_out;

  _32bit u_32bit_1 (.Add_Sub_control(ALUCtl[2]), .in_2(A), .in_3(B), .out_4(n32bit_1_out_4));  // open: carry_out
  xor xor_1 (xor_1_out, ALUCtl[2], B[31]);
  not not_1 (not_1_out, A[31]);
  assign OR_out = A | B;  // OR_Gate OR, 32 bits wide
  assign AND_out = A & B;  // AND_Gate AND, 32 bits wide
  Comparator #(.width(32)) comparator_1 (.a(A), .b(B), .lt(comparator_1_lt));  // open: gt, eq
  not not_2 (not_2_out, xor_1_out);
  Shifter #(.width(32)) shifter_1 (.in(B), .\dist (SHamt), .out(shifter_1_out));
  Shifter #(.width(32), .shift("lr")) shifter_2 (.in(B), .\dist (SHamt), .out(shifter_2_out));
  assign not_3_out = ~OR_out;  // NOT_Gate not_3, 32 bits wide
  assign bit_extender_1_out = {{31{1'b0}}, comparator_1_lt};  // Bit_Extender bit_extender_1
  Multiplexer #(.width(32), .enable("false")) multiplexer_1 (
    .in0(AND_out), .in1(OR_out), .out(multiplexer_1_out), .sel(ALUCtl[0]));
  not not_4 (not_4_out, n32bit_1_out_4[31]);
  and and_2 (and_2_out, A[31], not_4_out, xor_1_out);
  and and_3 (and_3_out, not_2_out, n32bit_1_out_4[31], not_1_out);
  Multiplexer #(.width(32), .enable("false")) multiplexer_2 (
    .in0(shifter_1_out), .in1(shifter_2_out), .out(multiplexer_2_out), .sel(ALUCtl[2]));
  Multiplexer #(.select(2), .width(32), .enable("false")) multiplexer_3 (
    .in0(multiplexer_1_out), .in1(multiplexer_4_out), .in2(not_3_out), .in3(multiplexer_2_out),
    .out(ALUResult), .sel({ALUCtl[3], ALUCtl[1]}));
  Multiplexer #(.width(32), .enable("false")) multiplexer_4 (
    .in0(n32bit_1_out_4), .in1(bit_extender_1_out), .out(multiplexer_4_out), .sel(ALUCtl[0]));
  or or_2 (or_2_out, and_2_out, and_3_out);
  not not_5 (not_5_out, ALUCtl[3]);
  not not_6 (not_6_out, ALUCtl[0]);
  and and_4 (Overflow, or_2_out, not_5_out, ALUCtl[1], not_6_out);
  or or_3 (or_3_out, ALUResult[0], ALUResult[1], ALUResult[2], ALUResult[3], ALUResult[4], ALUResult[5], ALUResult[6], ALUResult[7], ALUResult[8], ALUResult[9], ALUResult[10], ALUResult[11], ALUResult[12], ALUResult[13], ALUResult[14], ALUResult[15], ALUResult[16], ALUResult[17], ALUResult[18], ALUResult[19], ALUResult[20], ALUResult[21], ALUResult[22], ALUResult[23], ALUResult[24], ALUResult[25], ALUResult[26], ALUResult[27], ALUResult[28], ALUResult[29], ALUResult[30], ALUResult[31]);
  not not_7 (Zero, or_3_out);

  // Other names for the same wires on the sheet: ALUCtl_1 = ALUCtl[1]; ALUCtl_3 = ALUCtl[3]; ALUCtl_0 = ALUCtl[0];
  //   ALUCtl_2 = ALUCtl[2]
endmodule

module RegisterFile (
  input  clock,
  input  [31:0] WriteData,
  input  [4:0] ReadReg2,
  input  RegWrite,
  input  [4:0] Read_Reg1,
  input  [4:0] WriteReg,
  output [31:0] Read_Data2,
  output [31:0] Read_Data1
);

  wire demultiplexer_1_out0, demultiplexer_1_out1, demultiplexer_1_out2, demultiplexer_1_out3,
       demultiplexer_1_out4, demultiplexer_1_out5, demultiplexer_1_out6, demultiplexer_1_out7,
       demultiplexer_1_out8, demultiplexer_1_out9, demultiplexer_1_out10, demultiplexer_1_out11,
       demultiplexer_1_out12, demultiplexer_1_out13, demultiplexer_1_out14, demultiplexer_1_out15,
       demultiplexer_1_out16, demultiplexer_1_out17, demultiplexer_1_out18, demultiplexer_1_out19,
       demultiplexer_1_out20, demultiplexer_1_out21, demultiplexer_1_out22, demultiplexer_1_out23,
       demultiplexer_1_out24, demultiplexer_1_out25, demultiplexer_1_out26, demultiplexer_1_out27,
       demultiplexer_1_out28, demultiplexer_1_out29, demultiplexer_1_out30, demultiplexer_1_out31;
  wire [31:0] Reg0_2_q, Reg0_3_q, Reg0_4_q, Reg0_5_q, Reg0_6_q, Reg0_7_q, Reg0_8_q, Reg0_9_q, Reg0_10_q,
       Reg0_11_q, Reg0_12_q, Reg0_13_q, Reg0_14_q, Reg0_15_q, Reg0_16_q, Reg0_17_q, Reg0_18_q, Reg0_19_q,
       Reg0_20_q, Reg0_21_q, Reg0_22_q, Reg0_23_q, Reg0_24_q, Reg0_25_q, Reg0_26_q, Reg0_27_q, Reg0_28_q,
       Reg0_29_q, Reg0_30_q, Reg0_31_q, Reg0_32_q, Reg0_q;

  Demultiplexer #(.select(5)) demultiplexer_1 (
    .out0(demultiplexer_1_out0), .out1(demultiplexer_1_out1), .out2(demultiplexer_1_out2),
    .out3(demultiplexer_1_out3), .out4(demultiplexer_1_out4), .out5(demultiplexer_1_out5),
    .out6(demultiplexer_1_out6), .out7(demultiplexer_1_out7), .out8(demultiplexer_1_out8),
    .out9(demultiplexer_1_out9), .out10(demultiplexer_1_out10), .out11(demultiplexer_1_out11),
    .out12(demultiplexer_1_out12), .out13(demultiplexer_1_out13), .out14(demultiplexer_1_out14),
    .out15(demultiplexer_1_out15), .out16(demultiplexer_1_out16), .out17(demultiplexer_1_out17),
    .out18(demultiplexer_1_out18), .out19(demultiplexer_1_out19), .out20(demultiplexer_1_out20),
    .out21(demultiplexer_1_out21), .out22(demultiplexer_1_out22), .out23(demultiplexer_1_out23),
    .out24(demultiplexer_1_out24), .out25(demultiplexer_1_out25), .out26(demultiplexer_1_out26),
    .out27(demultiplexer_1_out27), .out28(demultiplexer_1_out28), .out29(demultiplexer_1_out29),
    .out30(demultiplexer_1_out30), .out31(demultiplexer_1_out31), .in(RegWrite), .sel(WriteReg));  // open: en
  Register #(.width(32)) Reg0 (.D(WriteData), .en(demultiplexer_1_out0), .Q(Reg0_q), .clk(clock));  // open: clr
  Register #(.width(32)) Reg0_2 (.D(WriteData), .en(demultiplexer_1_out4), .Q(Reg0_2_q), .clk(clock));  // open: clr
  Register #(.width(32)) Reg0_3 (.D(WriteData), .en(demultiplexer_1_out8), .Q(Reg0_3_q), .clk(clock));  // open: clr
  Register #(.width(32)) Reg0_4 (.D(WriteData), .en(demultiplexer_1_out12), .Q(Reg0_4_q), .clk(clock));  // open: clr
  Register #(.width(32)) Reg0_5 (.D(WriteData), .en(demultiplexer_1_out16), .Q(Reg0_5_q), .clk(clock));  // open: clr
  Register #(.width(32)) Reg0_6 (.D(WriteData), .en(demultiplexer_1_out20), .Q(Reg0_6_q), .clk(clock));  // open: clr
  Register #(.width(32)) Reg0_7 (.D(WriteData), .en(demultiplexer_1_out24), .Q(Reg0_7_q), .clk(clock));  // open: clr
  Register #(.width(32)) Reg0_8 (.D(WriteData), .en(demultiplexer_1_out28), .Q(Reg0_8_q), .clk(clock));  // open: clr
  Register #(.width(32)) Reg0_9 (.D(WriteData), .en(demultiplexer_1_out1), .Q(Reg0_9_q), .clk(clock));  // open: clr
  Register #(.width(32)) Reg0_10 (.D(WriteData), .en(demultiplexer_1_out5), .Q(Reg0_10_q), .clk(clock));  // open: clr
  Register #(.width(32)) Reg0_11 (.D(WriteData), .en(demultiplexer_1_out9), .Q(Reg0_11_q), .clk(clock));  // open: clr
  Register #(.width(32)) Reg0_12 (.D(WriteData), .en(demultiplexer_1_out13), .Q(Reg0_12_q), .clk(clock));  // open: clr
  Register #(.width(32)) Reg0_13 (.D(WriteData), .en(demultiplexer_1_out17), .Q(Reg0_13_q), .clk(clock));  // open: clr
  Register #(.width(32)) Reg0_14 (.D(WriteData), .en(demultiplexer_1_out21), .Q(Reg0_14_q), .clk(clock));  // open: clr
  Register #(.width(32)) Reg0_15 (.D(WriteData), .en(demultiplexer_1_out25), .Q(Reg0_15_q), .clk(clock));  // open: clr
  Register #(.width(32)) Reg0_16 (.D(WriteData), .en(demultiplexer_1_out29), .Q(Reg0_16_q), .clk(clock));  // open: clr
  Register #(.width(32)) Reg0_17 (.D(WriteData), .en(demultiplexer_1_out2), .Q(Reg0_17_q), .clk(clock));  // open: clr
  Register #(.width(32)) Reg0_18 (.D(WriteData), .en(demultiplexer_1_out6), .Q(Reg0_18_q), .clk(clock));  // open: clr
  Register #(.width(32)) Reg0_19 (.D(WriteData), .en(demultiplexer_1_out10), .Q(Reg0_19_q), .clk(clock));  // open: clr
  Register #(.width(32)) Reg0_20 (.D(WriteData), .en(demultiplexer_1_out14), .Q(Reg0_20_q), .clk(clock));  // open: clr
  Register #(.width(32)) Reg0_21 (.D(WriteData), .en(demultiplexer_1_out18), .Q(Reg0_21_q), .clk(clock));  // open: clr
  Register #(.width(32)) Reg0_22 (.D(WriteData), .en(demultiplexer_1_out22), .Q(Reg0_22_q), .clk(clock));  // open: clr
  Register #(.width(32)) Reg0_23 (.D(WriteData), .en(demultiplexer_1_out26), .Q(Reg0_23_q), .clk(clock), .clr(clock));
  Register #(.width(32)) Reg0_24 (.D(WriteData), .en(demultiplexer_1_out30), .Q(Reg0_24_q), .clk(clock));  // open: clr
  Register #(.width(32)) Reg0_25 (.D(WriteData), .en(demultiplexer_1_out3), .Q(Reg0_25_q), .clk(clock));  // open: clr
  Register #(.width(32)) Reg0_26 (.D(WriteData), .en(demultiplexer_1_out7), .Q(Reg0_26_q), .clk(clock));  // open: clr
  Register #(.width(32)) Reg0_27 (.D(WriteData), .en(demultiplexer_1_out11), .Q(Reg0_27_q), .clk(clock));  // open: clr
  Register #(.width(32)) Reg0_28 (.D(WriteData), .en(demultiplexer_1_out15), .Q(Reg0_28_q), .clk(clock));  // open: clr
  Register #(.width(32)) Reg0_29 (.D(WriteData), .en(demultiplexer_1_out19), .Q(Reg0_29_q), .clk(clock));  // open: clr
  Register #(.width(32)) Reg0_30 (.D(WriteData), .en(demultiplexer_1_out23), .Q(Reg0_30_q), .clk(clock));  // open: clr
  Register #(.width(32)) Reg0_31 (.D(WriteData), .en(demultiplexer_1_out27), .Q(Reg0_31_q), .clk(clock));  // open: clr
  Register #(.width(32)) Reg0_32 (.D(WriteData), .en(demultiplexer_1_out31), .Q(Reg0_32_q), .clk(clock));  // open: clr
  Multiplexer #(.select(5), .width(32)) multiplexer_1 (
    .in0(Reg0_q), .in1(Reg0_9_q), .in2(Reg0_17_q), .in3(Reg0_25_q), .in4(Reg0_2_q), .in5(Reg0_10_q),
    .in6(Reg0_18_q), .in7(Reg0_26_q), .in8(Reg0_3_q), .in9(Reg0_11_q), .in10(Reg0_19_q), .in11(Reg0_27_q),
    .in12(Reg0_4_q), .in13(Reg0_12_q), .in14(Reg0_20_q), .in15(Reg0_28_q), .in16(Reg0_5_q), .in17(Reg0_13_q),
    .in18(Reg0_21_q), .in19(Reg0_29_q), .in20(Reg0_6_q), .in21(Reg0_14_q), .in22(Reg0_22_q),
    .in23(Reg0_30_q), .in24(Reg0_7_q), .in25(Reg0_15_q), .in26(Reg0_23_q), .in27(Reg0_31_q), .in28(Reg0_8_q),
    .in29(Reg0_16_q), .in30(Reg0_24_q), .in31(Reg0_32_q), .out(Read_Data1), .sel(Read_Reg1));  // open: en
  Multiplexer #(.select(5), .width(32)) multiplexer_2 (
    .in0(Reg0_q), .in1(Reg0_9_q), .in2(Reg0_17_q), .in3(Reg0_25_q), .in4(Reg0_2_q), .in5(Reg0_10_q),
    .in6(Reg0_18_q), .in7(Reg0_26_q), .in8(Reg0_3_q), .in9(Reg0_11_q), .in10(Reg0_19_q), .in11(Reg0_27_q),
    .in12(Reg0_4_q), .in13(Reg0_12_q), .in14(Reg0_20_q), .in15(Reg0_28_q), .in16(Reg0_5_q), .in17(Reg0_13_q),
    .in18(Reg0_21_q), .in19(Reg0_29_q), .in20(Reg0_6_q), .in21(Reg0_14_q), .in22(Reg0_22_q),
    .in23(Reg0_30_q), .in24(Reg0_7_q), .in25(Reg0_15_q), .in26(Reg0_23_q), .in27(Reg0_31_q), .in28(Reg0_8_q),
    .in29(Reg0_16_q), .in30(Reg0_24_q), .in31(Reg0_32_q), .out(Read_Data2), .sel(ReadReg2));  // open: en
endmodule
